// Logisim project Guess the number Xtreme.circ as structural Verilog: 3 circuits, main circuit main
module main (
  input  in_1,
  input  in_2,
  input  in_3,
  input  in_4,
  input  in_5,
  input  in_6,
  input  in_7,
  input  in_8
);

  wire A_JOGANDO, A_VENCEU, ACERTOU, and_1_out, and_2_out, and_3_out, B_JOGANDO, B_VENCEU, CHUTANDO_S,
       CHUTANDO_X, CHUTANDO_Y, CHUTAR, clearA, clearB, clk, comparator_1_eq, comparator_2_eq,
       comparator_3_eq, comparator_4_eq, comparator_5_eq, comparator_6_eq, CONFIGURAR, dm, dmA_t, dmB_t, ds,
       dsA_t, dsB_t, EMPATE, endA, endB, FIM_DE_JOGO, IGUAL, MAIOR, MENOR, not_2_out, not_3_out,
       \NOVO_NÚMERO , or_1_out, or_2_out, or_3_out, PAUSAR, \PRÓXIMO , RESET, SA, SB, SC, Sinal_A, Sinal_B,
       START, START_A, tunnel, um, umA_t, umB_t, us, usA_t, usB_t, ZERAR_TIMER, zerar_timer_A, zerar_timer_B;
  wire [3:0] adder_1_out, adder_2_out, DMA, DMB, DSA, DSB, PA, PB, UMA, UMB, USA, USB, XC, YC;

  Clock clock_1 (.out(clk));
  Button button_1 (.out(dmA_t));
  Hex_Digit_Display hex_digit_display_1 (.value(DMA));  // open: dp
  core Core (
    .A({in_5, in_6, in_7, in_8}), .B({in_1, in_2, in_3, in_4}), .Adead(endA), .reset(RESET),
    .proximo(\PRÓXIMO ), .chutar(CHUTAR), .maior(MAIOR), .X(CHUTANDO_X), .Y(CHUTANDO_Y), .Xc(XC), .Yc(YC),
    .turn(A_JOGANDO), .acertou(ACERTOU), .pause(PAUSAR), .start(START), .mode(CONFIGURAR), .ended(or_1_out),
    .Sc(SC), .S(CHUTANDO_S), .SAi(Sinal_A), .SBi(Sinal_B), .igual(IGUAL), .menor(MENOR), .Bdead(endB),
    .SAo(SA), .SBo(SB), .aleatoriador(\NOVO_NÚMERO ));
  and and_1 (and_1_out, endA, endB);
  or or_1 (or_1_out, and_1_out, ACERTOU);
  and and_2 (and_2_out, A_JOGANDO, ACERTOU);
  Hex_Digit_Display hex_digit_display_2 (.value(PA));  // open: dp
  Button button_2 (.out(umA_t));
  LED led_1 (.in(1'b1));
  LED led_2 (.in(1'b1));
  Hex_Digit_Display hex_digit_display_3 (.value(UMA));  // open: dp
  LED led_3 (.in(SA));
  Button button_3 (.out(Sinal_A));
  LED led_4 (.in(A_JOGANDO));
  or or_2 (or_2_out, PAUSAR, B_JOGANDO);
  D_Flip_Flop d_ff_1 (.clk(and_2_out), .D(adder_1_out[3]), .Q(PA[3]), .reset(RESET));  // open: Qn, preset, en
  Button button_4 (.out(dsA_t));
  Hex_Digit_Display hex_digit_display_4 (.value(DSA));  // open: dp
  Hex_Digit_Display hex_digit_display_5 (.value({in_5, in_6, in_7, in_8}));  // open: dp
  \cronômetro  Timer_A (
    .mode(CONFIGURAR), .clear(clearA), .clk(clk), .pauseX(or_2_out), .start(START_A), .DMX(DMA), .UMX(UMA),
    .DSX(DSA), .USX(USA), .dm(dm), .um(um), .ds(ds), .us(us), .endX(endA), .configON(tunnel));
  not not_1 (B_JOGANDO, A_JOGANDO);
  D_Flip_Flop d_ff_2 (.clk(and_2_out), .D(adder_1_out[2]), .Q(PA[2]), .reset(RESET));  // open: Qn, preset, en
  Button button_5 (.out(usA_t));
  Hex_Digit_Display hex_digit_display_6 (.value(USA));  // open: dp
  D_Flip_Flop d_ff_3 (.clk(and_2_out), .D(adder_1_out[1]), .Q(PA[1]), .reset(RESET));  // open: Qn, preset, en
  or or_3 (or_3_out, PAUSAR, A_JOGANDO);
  D_Flip_Flop d_ff_4 (.clk(and_2_out), .D(adder_1_out[0]), .Q(PA[0]), .reset(RESET));  // open: Qn, preset, en
  LED led_5 (.in(A_VENCEU));
  Button button_6 (.out(START));
  Button button_7 (.out(zerar_timer_A));
  LED led_6 (.in(MENOR));
  LED led_7 (.in(SC));
  LED led_8 (.in(CHUTANDO_S));
  or or_4 (START_A, START, A_JOGANDO);
  Adder #(.width(4)) adder_1 (.a(PA), .b(4'b0001), .out(adder_1_out));  // open: cin, cout
  Button button_8 (.out(\NOVO_NÚMERO ));
  LED led_9 (.in(FIM_DE_JOGO));
  LED led_10 (.in(EMPATE));
  LED led_11 (.in(tunnel));
  Button button_9 (.out(CONFIGURAR));
  Button button_10 (.out(ZERAR_TIMER));
  Button button_11 (.out(PAUSAR));
  LED led_12 (.in(ACERTOU));
  LED led_13 (.in(IGUAL));
  Button button_12 (.out(\PRÓXIMO ));
  Hex_Digit_Display hex_digit_display_7 (.value(XC));  // open: dp
  LED led_14 (.in(CHUTANDO_X));
  \cronômetro  Timer_A_2 (
    .mode(CONFIGURAR), .clear(clearB), .clk(clk), .pauseX(or_3_out), .start(B_JOGANDO), .DMX(DMB), .UMX(UMB),
    .DSX(DSB), .USX(USB), .dm(dm), .um(um), .ds(ds), .us(us), .endX(endB), .configON(tunnel));
  LED led_15 (.in(B_VENCEU));
  Button button_13 (.out(RESET));
  Button button_14 (.out(zerar_timer_B));
  LED led_16 (.in(MAIOR));
  Button button_15 (.out(CHUTAR));
  Hex_Digit_Display hex_digit_display_8 (.value(YC));  // open: dp
  or or_5 (clearA, zerar_timer_A, ZERAR_TIMER);
  or or_6 (clearB, ZERAR_TIMER, zerar_timer_B);
  and and_3 (and_3_out, B_JOGANDO, ACERTOU);
  LED led_17 (.in(CHUTANDO_Y));
  or or_7 (dm, dmA_t, dmB_t);
  D_Flip_Flop d_ff_5 (.clk(and_3_out), .D(adder_2_out[3]), .Q(PB[3]), .reset(RESET));  // open: Qn, preset, en
  or or_8 (um, umA_t, umB_t);
  Comparator #(.width(4), .mode("unsigned")) comparator_1 (.a(PA), .b(4'b1111), .eq(comparator_1_eq));  // open: gt, lt
  Comparator #(.width(4), .mode("unsigned")) comparator_2 (.a(PB), .b(4'b1111), .eq(comparator_2_eq));  // open: gt, lt
  not not_2 (not_2_out, comparator_2_eq);
  Comparator #(.width(4), .mode("unsigned")) comparator_3 (.a(PA), .b(4'b1111), .eq(comparator_3_eq));  // open: gt, lt
  Comparator #(.width(4), .mode("unsigned")) comparator_4 (.a(PB), .b(4'b1111), .eq(comparator_4_eq));  // open: gt, lt
  Comparator #(.width(4), .mode("unsigned")) comparator_5 (.a(PA), .b(4'b1111), .eq(comparator_5_eq));  // open: gt, lt
  not not_3 (not_3_out, comparator_5_eq);
  Comparator #(.width(4), .mode("unsigned")) comparator_6 (.a(PB), .b(4'b1111), .eq(comparator_6_eq));  // open: gt, lt
  D_Flip_Flop d_ff_6 (.clk(and_3_out), .D(adder_2_out[2]), .Q(PB[2]), .reset(RESET));  // open: Qn, preset, en
  Button button_16 (.out(umB_t));
  Button button_17 (.out(dmB_t));
  Hex_Digit_Display hex_digit_display_9 (.value(UMB));  // open: dp
  Hex_Digit_Display hex_digit_display_10 (.value(DMB));  // open: dp
  Button button_18 (.out(Sinal_B));
  or or_9 (ds, dsA_t, dsB_t);
  and and_4 (A_VENCEU, comparator_1_eq, not_2_out);
  and and_5 (EMPATE, comparator_3_eq, comparator_4_eq);
  and and_6 (B_VENCEU, not_3_out, comparator_6_eq);
  D_Flip_Flop d_ff_7 (.clk(and_3_out), .D(adder_2_out[1]), .Q(PB[1]), .reset(RESET));  // open: Qn, preset, en
  Hex_Digit_Display hex_digit_display_11 (.value(PB));  // open: dp
  LED led_18 (.in(1'b1));
  LED led_19 (.in(1'b1));
  LED led_20 (.in(SB));
  Hex_Digit_Display hex_digit_display_12 (.value({in_1, in_2, in_3, in_4}));  // open: dp
  LED led_21 (.in(B_JOGANDO));
  or or_10 (us, usA_t, usB_t);
  Button button_19 (.out(dsB_t));
  Button button_20 (.out(usB_t));
  Hex_Digit_Display hex_digit_display_13 (.value(DSB));  // open: dp
  Hex_Digit_Display hex_digit_display_14 (.value(USB));  // open: dp
  D_Flip_Flop d_ff_8 (.clk(and_3_out), .D(adder_2_out[0]), .Q(PB[0]), .reset(RESET));  // open: Qn, preset, en
  Adder #(.width(4)) adder_2 (.a(PB), .b(4'b0001), .out(adder_2_out));  // open: cin, cout

  // Other names for the same wires on the sheet: A[3:0] = {in_5, in_6, in_7, in_8}; A0 = in_8; A1 = in_7; A2 = in_6;
  //   A3 = in_5; B[3:0] = {in_1, in_2, in_3, in_4}; B0 = in_4; B1 = in_3; B2 = in_2; B3 = in_1; PAUSAR_A = B_JOGANDO;
  //   START_B = B_JOGANDO; PAUSAR_B = A_JOGANDO; turn = A_JOGANDO

  // Notes on the sheet:
  //   NÃO CHUTE -00
  //   O led de sinal ligado significa NEGATIVO
  //   JOGADOR A
  //   PLACAR
  //   CRONÔMETRO
  //   O número secreto é
  //   JOGADOR B
  //   PLACAR
  //   CRONÔMETRO
endmodule

module core (
  input  aleatoriador,
  input  mode,
  input  SAi,
  input  [3:0] A,
  input  [3:0] B,
  input  SBi,
  input  Adead,
  input  Bdead,
  input  ended,
  input  pause,
  input  start,
  input  chutar,
  input  reset,
  input  proximo,
  output Sc,
  output turn,
  output S,
  output X,
  output Y,
  output [3:0] Xc,
  output [3:0] Yc,
  output SBo,
  output SAo,
  output maior,
  output igual,
  output acertou,
  output menor
);

  wire and_1_out, and_2_out, and_3_out, and_7_out, and_8_out, and_9_out, and_10_out, and_11_out, and_12_out,
       and_16_out, and_17_out, and_18_out, and_19_out, Answerturn, comparator_1_eq, comparator_1_gt,
       comparator_1_lt, comparator_2_eq, comparator_2_gt, comparator_2_lt, d_ff_1_qn, d_ff_2_qn, d_ff_4_q,
       jogando, maior_t, menor_t, mode_t, multiplexer_1_out, not_1_out, not_2_out, not_3_out, not_5_out,
       not_6_out, not_7_out, not_8_out, not_9_out, not_10_out, not_12_out, or_3_out, or_4_out, or_5_out,
       or_6_out, or_7_out, or_8_out, pausado_ou_acabado, paused, proximo_t, SA, SB, Ss, xnor_1_out;
  wire [2:0] adder_1_out, fase;
  wire [3:0] bit_extender_1_out, multiplexer_2_out, multiplexer_3_out, Xs, Ys;

  or or_1 (pausado_ou_acabado, paused, ended);
  Random #(.width(1)) random_1 (.clk(aleatoriador), .out(Ss));  // open: next, clr
  D_Flip_Flop d_ff_1 (.clk(SAi), .D(d_ff_1_qn), .Q(SA), .Qn(d_ff_1_qn));  // open: preset, en, reset
  D_Flip_Flop d_ff_2 (.clk(SBi), .D(d_ff_2_qn), .Q(SB), .Qn(d_ff_2_qn));  // open: preset, en, reset
  Multiplexer multiplexer_1 (.in0(pause), .in1(start), .out(multiplexer_1_out), .sel(pausado_ou_acabado));  // open: en
  and and_1 (and_1_out, Adead, not_1_out);
  not not_1 (not_1_out, Bdead);
  Adder #(.width(3)) adder_1 (.a(fase), .b(3'b001), .out(adder_1_out));  // open: cin, cout
  Random random_2 (.clk(aleatoriador), .out({Ys, Xs}));  // open: next, clr
  D_Flip_Flop d_ff_3 (.clk(mode), .D(not_2_out), .Q(mode_t));  // open: Qn, preset, en, reset
  not not_2 (not_2_out, mode_t);
  D_Flip_Flop d_ff_4 (.clk(multiplexer_1_out), .D(not_3_out), .Q(d_ff_4_q));  // open: Qn, preset, en, reset
  not not_3 (not_3_out, paused);
  not not_4 (jogando, pausado_ou_acabado);
  and and_2 (and_2_out, proximo_t, jogando);
  Multiplexer #(.width(4)) multiplexer_2 (.in0(A), .in1(B), .out(multiplexer_2_out), .sel(fase[2]));  // open: en
  or or_2 (paused, mode_t, d_ff_4_q);
  D_Flip_Flop d_ff_5 (
    .clk(and_2_out), .D(adder_1_out[2]), .Q(fase[2]), .preset(and_1_out), .reset(or_3_out));  // open: Qn, en
  or or_3 (or_3_out, reset, and_7_out, or_7_out);
  D_Flip_Flop d_ff_6 (.clk(and_2_out), .D(adder_1_out[1]), .Q(fase[1]), .reset(or_4_out));  // open: Qn, preset, en
  or or_4 (or_4_out, reset, or_7_out);
  D_Flip_Flop d_ff_7 (.clk(and_2_out), .D(adder_1_out[0]), .Q(fase[0]), .reset(or_5_out));  // open: Qn, preset, en
  or or_5 (or_5_out, reset, or_7_out);
  and and_3 (and_3_out, chutar, jogando, X);
  and and_4 (SBo, fase[2], SB);
  and and_5 (SAo, turn, SA);
  D_Flip_Flop d_ff_8 (.clk(and_3_out), .D(multiplexer_2_out[3]), .Q(Xc[3]));  // open: Qn, preset, en, reset
  D_Flip_Flop d_ff_9 (.clk(and_3_out), .D(multiplexer_2_out[2]), .Q(Xc[2]));  // open: Qn, preset, en, reset
  D_Flip_Flop d_ff_10 (.clk(and_3_out), .D(multiplexer_2_out[1]), .Q(Xc[1]));  // open: Qn, preset, en, reset
  D_Flip_Flop d_ff_11 (.clk(and_3_out), .D(multiplexer_2_out[0]), .Q(Xc[0]));  // open: Qn, preset, en, reset
  and and_6 (proximo_t, jogando, or_6_out);
  or or_6 (or_6_out, reset, proximo);
  and and_7 (and_7_out, not_5_out, Bdead);
  or or_7 (or_7_out, ended, and_10_out);
  and and_8 (and_8_out, S, chutar);
  or or_8 (or_8_out, SBo, SAo);
  Multiplexer #(.width(4)) multiplexer_3 (.in0(A), .in1(B), .out(multiplexer_3_out), .sel(fase[2]));  // open: en
  and and_9 (and_9_out, chutar, jogando, Y);
  not not_5 (not_5_out, Adead);
  and and_10 (and_10_out, Adead, Bdead);
  D_Flip_Flop d_ff_12 (.clk(and_8_out), .D(or_8_out), .Q(Sc));  // open: Qn, preset, en, reset
  D_Flip_Flop d_ff_13 (.clk(and_9_out), .D(multiplexer_3_out[3]), .Q(Yc[3]));  // open: Qn, preset, en, reset
  D_Flip_Flop d_ff_14 (.clk(and_9_out), .D(multiplexer_3_out[2]), .Q(Yc[2]));  // open: Qn, preset, en, reset
  D_Flip_Flop d_ff_15 (.clk(and_9_out), .D(multiplexer_3_out[1]), .Q(Yc[1]));  // open: Qn, preset, en, reset
  D_Flip_Flop d_ff_16 (.clk(and_9_out), .D(multiplexer_3_out[0]), .Q(Yc[0]));  // open: Qn, preset, en, reset
  xnor xnor_1 (xnor_1_out, Sc, Ss);
  and and_11 (and_11_out, Sc, not_6_out);
  not not_6 (not_6_out, Ss);
  not not_7 (not_7_out, Sc);
  and and_12 (and_12_out, not_7_out, Ss);
  Comparator #(.width(4), .mode("unsigned")) comparator_1 (
    .a(Xs), .b(Xc), .gt(comparator_1_gt), .eq(comparator_1_eq), .lt(comparator_1_lt));
  Comparator #(.width(4), .mode("unsigned")) comparator_2 (
    .a(Ys), .b(Yc), .gt(comparator_2_gt), .eq(comparator_2_eq), .lt(comparator_2_lt));
  and and_13 (maior, maior_t, Answerturn);
  and and_14 (igual, acertou, Answerturn);
  and and_15 (menor, menor_t, Answerturn);
  and and_16 (and_16_out, xnor_1_out, comparator_1_eq, comparator_2_gt);
  and and_17 (and_17_out, xnor_1_out, comparator_1_gt);
  and and_18 (and_18_out, xnor_1_out, comparator_1_eq, comparator_2_lt);
  and and_19 (and_19_out, xnor_1_out, comparator_1_lt);
  Hex_Digit_Display hex_digit_display_1 (.value(bit_extender_1_out));  // open: dp
  assign bit_extender_1_out = {{1{1'b0}}, fase};  // Bit_Extender bit_extender_1
  or or_9 (maior_t, and_16_out, and_17_out, and_11_out);
  and and_20 (acertou, xnor_1_out, comparator_1_eq, comparator_2_eq);
  or or_10 (menor_t, and_18_out, and_19_out, and_12_out);
  not not_8 (not_8_out, fase[1]);
  not not_9 (not_9_out, fase[0]);
  not not_10 (not_10_out, fase[1]);
  not not_11 (turn, fase[2]);
  and and_21 (S, not_8_out, not_9_out);
  and and_22 (X, not_10_out, fase[0]);
  and and_23 (Y, fase[1], not_12_out);
  not not_12 (not_12_out, fase[0]);
  and and_24 (Answerturn, fase[1], fase[0]);

  // Other names for the same wires on the sheet: turnB = fase[2]; game_over = ended; igual_t = acertou; Sturn = S;
  //   turnA = turn; Xturn = X; Yturn = Y
endmodule

module \cronômetro  (
  input  mode,
  input  clear,
  input  clk,
  input  pauseX,
  input  start,
  input  dm,
  input  um,
  input  ds,
  input  us,
  output endX,
  output [3:0] DMX,
  output [3:0] UMX,
  output [3:0] DSX,
  output [3:0] USX,
  output configON
);

  wire and_5_out, and_6_out, d_ff_1_q, DMX___0, DMX___F, DMX_t, DSX___0, DSX___5, DSX___F, DSX_t, mudador,
       multiplexer_1_out, not_1_out, not_2_out, pausado_ou_acabado, paused, UMX___0, UMX___9, UMX___F, UMX_t,
       USX___0, USX___9, USX___F, USX_t;

  Multiplexer multiplexer_1 (.in0(pauseX), .in1(start), .out(multiplexer_1_out), .sel(pausado_ou_acabado));  // open: en
  and and_1 (DMX___F, DMX[3], DMX[2], DMX[1], DMX[0]);
  not not_1 (not_1_out, paused);
  and and_2 (DSX___F, DSX[3], DSX[2], DSX[1], DSX[0]);
  and and_3 (UMX___F, UMX[3], UMX[2], UMX[1], UMX[0]);
  Multiplexer multiplexer_2 (.in0(clk), .in1(1'b0), .out(mudador), .sel(pausado_ou_acabado));  // open: en
  not not_2 (not_2_out, configON);
  D_Flip_Flop d_ff_1 (.clk(multiplexer_1_out), .D(not_1_out), .Q(d_ff_1_q));  // open: Qn, preset, en, reset
  and and_4 (USX___F, USX[3], USX[2], USX[1], USX[0]);
  D_Flip_Flop d_ff_2 (.clk(mode), .D(not_2_out), .Q(configON));  // open: Qn, preset, en, reset
  or or_1 (paused, configON, d_ff_1_q);
  Counter #(.width(4), .max('h5)) counter_1 (
    .load(1'b1), .D(DMX), .Q(DMX), .carry(DMX___0), .clk(DMX_t), .clr(clear));  // open: count
  or or_2 (pausado_ou_acabado, paused, endX);
  Counter #(.width(4), .max('h9)) counter_2 (
    .load(1'b1), .D(UMX), .Q(UMX), .carry(UMX___0), .clk(UMX_t), .clr(clear));  // open: count
  Counter #(.width(4), .max('h5)) counter_3 (
    .load(1'b1), .D(DSX), .Q(DSX), .carry(DSX___0), .clk(DSX_t), .clr(clear));  // open: count
  and and_5 (and_5_out, UMX___0, DSX___0, USX___0);
  and and_6 (and_6_out, DSX___0, USX___0);
  D_Flip_Flop d_ff_3 (.clk(mudador), .D(and_5_out), .Q(UMX___9));  // open: Qn, preset, en, reset
  D_Flip_Flop d_ff_4 (.clk(mudador), .D(and_6_out), .Q(DSX___5));  // open: Qn, preset, en, reset
  D_Flip_Flop d_ff_5 (.clk(mudador), .D(USX___0), .Q(USX___9));  // open: Qn, preset, en, reset
  Counter #(.width(4), .max('h9)) counter_4 (
    .load(1'b1), .D(USX), .Q(USX), .carry(USX___0), .clk(USX_t), .clr(clear));  // open: count
  and and_7 (endX, DMX___0, UMX___0, DSX___0, USX___0);
  Multiplexer multiplexer_3 (.in0(UMX___9), .in1(dm), .out(DMX_t), .sel(configON));  // open: en
  Multiplexer multiplexer_4 (.in0(DSX___5), .in1(um), .out(UMX_t), .sel(configON));  // open: en
  Multiplexer multiplexer_5 (.in0(USX___9), .in1(ds), .out(DSX_t), .sel(configON));  // open: en
  Multiplexer multiplexer_6 (.in0(mudador), .in1(us), .out(USX_t), .sel(configON));  // open: en

  // Other names for the same wires on the sheet: game_over = endX; mode_t = configON
endmodule
